# Fritzing sketch Electronic skech (saved by Fritzing 0.9.5d)
breadboards: 2

parts:
  U1 = LuaNode32 / ESP32 [part_number=ESP32S-PIN30]
  hc-sr1 = hc-sr04
  U2 = LuaNode32 / ESP32 [part_number=ESP32S-PIN30]
  RHT1 = Humidity and Temperature Sensor RHT03
  R2 = Resistor [tolerance=±5% resistance=10k package="2512 [SMD]"]
  LCD1 = 2.8" SPI TFT Module [part_number=MSP2807]

nets:
  VCC: U1.3V3, hc-sr1.VCC, RHT1.Vcc, R2.Pin_0
  GND: U1.GND, hc-sr1.GND, RHT1.GND_2
  N1: U1.D4, RHT1.Data-signal, R2.Pin_1
  N2: U1.D5, hc-sr1.Trig
  N3: U1.D18, hc-sr1.Echo
  N4: U2.EN, LCD1.pin4
  N5: U2.VN, LCD1.pin13
  N6: U2.D32, LCD1.pin12
  N7: U2.D33, LCD1.pin11
  N8: U2.D25, LCD1.pin10
  N9: U2.D14, LCD1.pin7
  N10: U2.D12, LCD1.pin9
  N11: U2.D13, LCD1.pin6
  N12: U2.GND, LCD1.pin2
  N13: U2.Vin, LCD1.pin1
  N14: U2.D15, LCD1.pin3
  N15: U2.D2, LCD1.pin5
  N16: U2.D21, LCD1.pin8

custom parts:
  LuaNode32 / ESP32: New Image for LuaNode32 DOIT ESP32 DEVKIT V1. Base parts from LuaNode32 / ESP32 ESP32 based LuaNode32 by G.Noorlander DOIT Esp32 DevKit v1 (30 pins long, 11 pins width) by Werner Rothschopf (modified by vanepp Dec 2018)
  2.8" SPI TFT Module: A generic 2.8 inch LCD TFT 320x240 display with touchscreen and SD card slot. Uses the ILI9341 controller, like the Adafruit displays of this size uses.
